# Fritzing sketch RFClicker (saved by Fritzing 0.9.4)
circuit board: 2.38948cm x 5.40924cm
breadboards: 1

parts:
  RFduinoSMD1 = RFduino SMD
  LED1 = LED - 5mm [color="Green (570nm)" package="5 mm [THT]"]
  VCC1 = Battery
  S1 = Pushbutton [package="[SMD]"]
  S2 = Pushbutton [package="[SMD]"]
  S3 = Pushbutton [package="[SMD]"]
  R1 = Resistor [tolerance=±5% resistance=100 package=THT]
  S4 = Pushbutton [package="[SMD]"]

nets:
  N1: RFduinoSMD1.gnd, VCC1.-, R1.Pin_0
  N2: RFduinoSMD1.vin, VCC1.+, S1.Pin_3, S1.Pin_4, S2.Pin_3, S2.Pin_4, S3.Pin_3, S3.Pin_4, S4.Pin_3, S4.Pin_4
  N3: RFduinoSMD1.gpio2, S1.Pin_1, S1.Pin_2
  N4: RFduinoSMD1.gpio3, S2.Pin_1, S2.Pin_2
  N5: RFduinoSMD1.gpio4, S3.Pin_1, S3.Pin_2
  N6: RFduinoSMD1.gpio5, S4.Pin_1, S4.Pin_2
  N7: RFduinoSMD1.gpio6, LED1.cathode
  N8: LED1.anode, R1.Pin_1
